# Fritzing sketch Sketch (saved by Fritzing 0.8.5b)

parts:
  Part1 = Arduino Uno (Rev3)
  Part3 = Triple Axis Accelerometer Breakout - ADXL345

nets:
  N1: Part1.A4/SDA, Part3.SDA
  N2: Part1.A5/SCL, Part3.SCL
  GND: Part1.GND, Part3.GND
  3V3: Part1.3V3, Part3.VCC
